// Logisim project Final project .p1.circ as structural Verilog: 3 circuits, main circuit main
// ALU
module main (
  input  B,
  input  A,
  input  Carry_IN,
  input  [1:0] in_4,
  input  Binvert,
  output out_6,
  output Carry_Out
);

  wire adder_1_out, and_1_out, multiplexer_1_out, not_1_out, or_1_out, xnor_1_out;

  not not_1 (not_1_out, B);
  Multiplexer multiplexer_1 (.in0(not_1_out), .in1(B), .out(multiplexer_1_out), .sel(Binvert));  // open: en
  and and_1 (and_1_out, A, multiplexer_1_out);
  or or_1 (or_1_out, A, multiplexer_1_out);
  xnor xnor_1 (xnor_1_out, A, multiplexer_1_out);
  Adder #(.width(1)) adder_1 (.a(A), .b(multiplexer_1_out), .out(adder_1_out), .cin(Carry_IN), .cout(Carry_Out));
  Multiplexer #(.select(2)) multiplexer_2 (
    .in0(and_1_out), .in1(or_1_out), .in2(xnor_1_out), .in3(adder_1_out), .out(out_6), .sel(in_4));  // open: en
endmodule

// 16 ALU
module ALU1 (
  input  Carry_IN,
  input  [15:0] A,
  input  [15:0] B,
  input  Binvert,
  input  [1:0] OP
);

  wire main_1_carry_out, main_2_carry_out, main_3_carry_out, main_4_carry_out, main_5_carry_out,
       main_6_carry_out, main_7_carry_out, main_8_carry_out, main_9_carry_out, main_10_carry_out,
       main_11_carry_out, main_12_carry_out, main_13_carry_out, main_14_carry_out, main_15_carry_out,
       main_16_carry_out, nor_1_out;
  wire [15:0] main_1_out_6;

  main main_1 (
    .out_6(main_1_out_6[0]), .Carry_Out(main_1_carry_out), .B(B[0]), .A(A[0]), .Carry_IN(Carry_IN),
    .Binvert(Binvert), .in_4(OP));
  main main_2 (
    .out_6(main_1_out_6[1]), .Carry_Out(main_2_carry_out), .B(B[1]), .A(A[1]), .Carry_IN(main_1_carry_out),
    .Binvert(Binvert), .in_4(OP));
  main main_3 (
    .out_6(main_1_out_6[2]), .Carry_Out(main_3_carry_out), .B(B[2]), .A(A[2]), .Carry_IN(main_2_carry_out),
    .Binvert(Binvert), .in_4(OP));
  main main_4 (
    .out_6(main_1_out_6[3]), .Carry_Out(main_4_carry_out), .B(B[3]), .A(A[3]), .Carry_IN(main_3_carry_out),
    .Binvert(Binvert), .in_4(OP));
  main main_5 (
    .out_6(main_1_out_6[4]), .Carry_Out(main_5_carry_out), .B(B[4]), .A(A[4]), .Carry_IN(main_4_carry_out),
    .Binvert(Binvert), .in_4(OP));
  main main_6 (
    .out_6(main_1_out_6[5]), .Carry_Out(main_6_carry_out), .B(B[5]), .A(A[5]), .Carry_IN(main_5_carry_out),
    .Binvert(Binvert), .in_4(OP));
  main main_7 (
    .out_6(main_1_out_6[6]), .Carry_Out(main_7_carry_out), .B(B[6]), .A(A[6]), .Carry_IN(main_6_carry_out),
    .Binvert(Binvert), .in_4(OP));
  main main_8 (
    .out_6(main_1_out_6[7]), .Carry_Out(main_8_carry_out), .B(B[7]), .A(A[7]), .Carry_IN(main_7_carry_out),
    .Binvert(Binvert), .in_4(OP));
  main main_9 (
    .out_6(main_1_out_6[8]), .Carry_Out(main_9_carry_out), .B(B[8]), .A(A[8]), .Carry_IN(OP[0]),
    .Binvert(Binvert), .in_4(OP));
  main main_10 (
    .out_6(main_1_out_6[9]), .Carry_Out(main_10_carry_out), .B(B[9]), .A(A[9]), .Carry_IN(main_9_carry_out),
    .Binvert(Binvert), .in_4(OP));
  main main_11 (
    .out_6(main_1_out_6[10]), .Carry_Out(main_11_carry_out), .B(B[10]), .A(A[10]),
    .Carry_IN(main_10_carry_out), .Binvert(Binvert), .in_4(OP));
  main main_12 (
    .out_6(main_1_out_6[11]), .Carry_Out(main_12_carry_out), .B(B[11]), .A(A[11]),
    .Carry_IN(main_11_carry_out), .Binvert(Binvert), .in_4(OP));
  main main_13 (
    .out_6(main_1_out_6[12]), .Carry_Out(main_13_carry_out), .B(B[12]), .A(A[12]),
    .Carry_IN(main_12_carry_out), .Binvert(Binvert), .in_4(OP));
  main main_14 (
    .out_6(main_1_out_6[13]), .Carry_Out(main_14_carry_out), .B(B[13]), .A(A[13]),
    .Carry_IN(main_13_carry_out), .Binvert(Binvert), .in_4(OP));
  main main_15 (
    .out_6(main_1_out_6[14]), .Carry_Out(main_15_carry_out), .B(B[14]), .A(A[14]),
    .Carry_IN(main_14_carry_out), .Binvert(Binvert), .in_4(OP));
  main main_16 (
    .out_6(main_1_out_6[15]), .Carry_Out(main_16_carry_out), .B(B[15]), .A(A[15]),
    .Carry_IN(main_15_carry_out), .Binvert(Binvert), .in_4(OP));
  nor nor_1 (nor_1_out, main_1_out_6[0], main_1_out_6[1], main_1_out_6[2], main_1_out_6[3], main_1_out_6[4], main_1_out_6[5], main_1_out_6[6], main_1_out_6[7], main_1_out_6[8], main_1_out_6[9], main_1_out_6[10], main_1_out_6[11], main_1_out_6[12], main_1_out_6[13], main_1_out_6[14], main_1_out_6[15]);
  // Pins of 1 and 2 bits meet at OP
endmodule

module ALU_16 (
  input  in_1,
  input  [15:0] A,
  input  [15:0] B,
  input  Binvert,
  input  [1:0] OP,
  output [15:0] Output_result,
  output Zero,
  output Carry_Out,
  output Overflow
);

  ALU1 alu1_1 (.Carry_IN(in_1), .A(A), .B(B), .Binvert(Binvert), .OP(OP));
endmodule
